# Fritzing sketch Demo Sketch (saved by Fritzing 0.9.3b)
breadboards: 1

parts:
  DFRobot-DFPlayer-Mini1 = DFRobot DFPlayer Mini [part_number=DFR0299]

nets:
  N1: DFRobot-DFPlayer-Mini1.GND-1, DFRobot-DFPlayer-Mini1.GND-2

notes:
  DFRobot DFPlayer Mini
